// Logisim project ttt_wkt.circ as structural Verilog: 1 circuit, main circuit main
module main (
);

  wire b1, b2, b3, b4, b5, b6, b7, b8, b9, clock_1_out, clock_2_out, clock_3_out, p1, p2, p3, p4, p5, p6, p7,
       p8, p9, Reset, Tie, Win;
  wire [3:0] register_1_q, rom_1_data, Xstate;
  wire [8:0] demultiplexer_1_out1, Omoves;

  Clock clock_1 (.out(clock_1_out));
  Clock clock_2 (.out(clock_2_out));
  // Probe on Omoves
  Register #(.width(4)) register_1 (.D(Xstate), .Q(register_1_q), .clk(clock_1_out), .clr(Reset));  // open: en
  J_K_Flip_Flop j_k_ff_1 (.J(p1), .clk(clock_2_out), .K(b1), .Q(Omoves[0]), .reset(Reset));  // open: Qn, preset, en
  J_K_Flip_Flop j_k_ff_2 (.J(p2), .clk(clock_2_out), .K(b2), .Q(Omoves[1]), .reset(Reset));  // open: Qn, preset, en
  J_K_Flip_Flop j_k_ff_3 (.J(p3), .clk(clock_2_out), .K(b3), .Q(Omoves[2]), .reset(Reset));  // open: Qn, preset, en
  J_K_Flip_Flop j_k_ff_4 (.J(p4), .clk(clock_2_out), .K(b4), .Q(Omoves[3]), .reset(Reset));  // open: Qn, preset, en
  J_K_Flip_Flop j_k_ff_5 (.J(p5), .clk(clock_2_out), .K(b5), .Q(Omoves[4]), .reset(Reset));  // open: Qn, preset, en
  J_K_Flip_Flop j_k_ff_6 (.J(p6), .clk(clock_2_out), .K(b6), .Q(Omoves[5]), .reset(Reset));  // open: Qn, preset, en
  J_K_Flip_Flop j_k_ff_7 (.J(p7), .clk(clock_2_out), .K(b7), .Q(Omoves[6]), .reset(Reset));  // open: Qn, preset, en
  J_K_Flip_Flop j_k_ff_8 (.J(p8), .clk(clock_2_out), .K(b8), .Q(Omoves[7]), .reset(Reset));  // open: Qn, preset, en
  J_K_Flip_Flop j_k_ff_9 (.J(p9), .clk(clock_2_out), .K(b9), .Q(Omoves[8]), .reset(Reset));  // open: Qn, preset, en
  // Probe on {register_1_q, Omoves}
  // Probe on {Xstate, rom_1_data}
  ROM #(.addrWidth(13)) rom_1 (.addr({register_1_q, Omoves}), .data({Xstate, rom_1_data}));  // open: sel
  Clock clock_3 (.out(clock_3_out));
  J_K_Flip_Flop j_k_ff_10 (
    .J(demultiplexer_1_out1[0]), .clk(clock_3_out), .K(1'b0), .Q(b1), .reset(Reset));  // open: Qn, preset, en
  J_K_Flip_Flop j_k_ff_11 (
    .J(demultiplexer_1_out1[1]), .clk(clock_3_out), .K(1'b0), .Q(b2), .reset(Reset));  // open: Qn, preset, en
  J_K_Flip_Flop j_k_ff_12 (
    .J(demultiplexer_1_out1[2]), .clk(clock_3_out), .K(1'b0), .Q(b3), .reset(Reset));  // open: Qn, preset, en
  J_K_Flip_Flop j_k_ff_13 (
    .J(demultiplexer_1_out1[3]), .clk(clock_3_out), .K(1'b0), .Q(b4), .reset(Reset));  // open: Qn, preset, en
  J_K_Flip_Flop j_k_ff_14 (
    .J(demultiplexer_1_out1[4]), .clk(clock_3_out), .K(1'b0), .Q(b5), .reset(Reset));  // open: Qn, preset, en
  J_K_Flip_Flop j_k_ff_15 (
    .J(demultiplexer_1_out1[5]), .clk(clock_3_out), .K(1'b0), .Q(b6), .reset(Reset));  // open: Qn, preset, en
  J_K_Flip_Flop j_k_ff_16 (
    .J(demultiplexer_1_out1[6]), .clk(clock_3_out), .K(1'b0), .Q(b7), .reset(Reset));  // open: Qn, preset, en
  J_K_Flip_Flop j_k_ff_17 (
    .J(demultiplexer_1_out1[7]), .clk(clock_3_out), .K(1'b0), .Q(b8), .reset(Reset));  // open: Qn, preset, en
  J_K_Flip_Flop j_k_ff_18 (
    .J(demultiplexer_1_out1[8]), .clk(clock_3_out), .K(1'b0), .Q(b9), .reset(Reset));  // open: Qn, preset, en
  Demultiplexer #(.select(4), .enable("false")) demultiplexer_1 (
    .out1(demultiplexer_1_out1[0]), .out2(demultiplexer_1_out1[1]), .out3(demultiplexer_1_out1[2]),
    .out4(demultiplexer_1_out1[3]), .out5(demultiplexer_1_out1[4]), .out6(demultiplexer_1_out1[5]),
    .out7(demultiplexer_1_out1[6]), .out8(demultiplexer_1_out1[7]), .out9(demultiplexer_1_out1[8]),
    .out14(Tie), .out15(Win), .in(1'b1), .sel(rom_1_data));  // open: out0, out10, out11, out12, out13
  LED led_1 (.in(Omoves[0]));
  Button button_1 (.out(p1));
  Button button_2 (.out(p4));
  LED led_2 (.in(Omoves[3]));
  LED led_3 (.in(Omoves[6]));
  Button button_3 (.out(p7));
  Button button_4 (.out(Reset));
  Button button_5 (.out(p2));
  LED led_4 (.in(b1));
  LED led_5 (.in(b4));
  Button button_6 (.out(p5));
  Button button_7 (.out(p8));
  LED led_6 (.in(b7));
  Button button_8 (.out(p3));
  LED led_7 (.in(b2));
  LED led_8 (.in(Omoves[1]));
  LED led_9 (.in(b5));
  LED led_10 (.in(Omoves[4]));
  Button button_9 (.out(p6));
  Button button_10 (.out(p9));
  LED led_11 (.in(Omoves[7]));
  LED led_12 (.in(b8));
  LED led_13 (.in(Tie));
  LED led_14 (.in(b3));
  LED led_15 (.in(Omoves[2]));
  LED led_16 (.in(b6));
  LED led_17 (.in(Omoves[5]));
  LED led_18 (.in(Omoves[8]));
  LED led_19 (.in(b9));
  LED led_20 (.in(Win));

  // Other names for the same wires on the sheet: u1 = Omoves[0]; u2 = Omoves[1]; u3 = Omoves[2]; u4 = Omoves[3];
  //   u5 = Omoves[4]; u6 = Omoves[5]; u7 = Omoves[6]; u8 = Omoves[7]; u9 = Omoves[8];
  //   Xmoves[8:0] = {b9, b8, b7, b6, b5, b4, b3, b2, b1}

  // Notes on the sheet:
  //   contents of rom_1 (hex, n*v repeats v):
  //   0 95 31 0 95 0 1 0 31 0 5 0 5 0 29 0 31 0 8 0 0 0 37 0 0 0 26 0 0 0 f 0 43 5*0 29 0 5 0 93 0 29 f f
  //   0 0 9 64 18 0 0 f 9*0 95 0 5 0 0 0 14 0 1 0 29 0 42 5*0 13 7*0 f 7*0 29 0 0 f 0 0 42 0 0 0 f 4*0 22
  //   14*0 12 0 5 0 0 0 14 0 0 0 93 0 29 12*0 9 0 0 0 e 4*0 93 0 0 9 f 0 42 0 f 0 9 e 0 0 0 22 0 0 f 13*0
  //   29 f 0 f 0 0 29 8*0 f 6*0 f 8*0 9 9 e 28*0 95 0 5 0 0 0 56 0 1 0 93 0 56 f 7 0 0 0 13 0 0 0 f 11*0
  //   93 5*0 93 0 f 7*0 f 15*0 88 5*0 88 0 8 0 f 11*0 f 8*0 f 8 5*0 f 0 e 23*0 c7 0 0 0 f 0 c7 0 f 0 7 0 e
  //   5*0 f 0 0 0 f 9*0 f 5*0 f 7*0 f 103*0 16 0 28 0 47 0 18 0 0 14 14 75 9*0 1f 0 0 14 9 58 19 18*0 15
  //   11*0 18 5*0 43 0 36 6*0 75 75 0 0 1f 39 0 0 0 1f 5*0 21 0 34 1e 12*0 12 87 0 0 87 0 15 0 87 4*0 16 0
  //   0 51 19 0 0 0 74 0 0 92 6 6*0 87 75 75 1f 19 74 7 5*0 5 0 0 0 42 74 0 0 74 11*0 39 14 0 1f 0 65 36 0
  //   11 0 1f 0 25 4*0 23 6*0 33 7*0 11 23 1f 0 25 0 0 0 33 7*0 33 19*0 16 52 b4 5*0 51 1f 4*0 18 0 0 0 1f
  //   0 92 0 36 0 0 0 1e 0 0 75 b7 1f 12*0 21 0 34 16*0 1f b4 0 36 11*0 34 14*0 1f 6*0 1f 23*0 87 0 0 1f
  //   b4 16 36 5*0 16 1e 10*0 1f 8*0 1f 1f 5*0 1f 7*0 1f 82*0 23 7*0 47 0 0 2f 11*0 28 0 0 0 17 4*0 47 0 0
  //   2f 0 25 47 91 0 2f 22*0 74 6*0 2f 15*0 33 7*0 2f 28 2f 0 0 0 91 7*0 23 22 38 16*0 74 8*0 2f 11*0 26
  //   9 0 0 61 7*0 2f 0 0 0 91 2f 0 0 2f 4*0 29 16*0 2f 0 2f 0 0 0 2f 0 0 0 2f 4*0 23 14*0 2f 23 0 0 2f 0
  //   0 0 2f 7*0 62 2e 17*0 74 0 0 26 15*0 17 0 0 0 33 5*0 23 42 47 5*0 91 2f 6*0 23 0 47 19*0 35 25*0 58
  //   28 28 2e 12*0 62 19*0 26 15 35 0 0 2f 0 0 61 7*0 61 0 0 0 61 7*0 47 2f 6*0 2f 7*0 62 81*0 31 0 0 0
  //   74 0 31 0 5 0 5 32 0 0 31 0 8 0 a7 0 37 0 16 5*0 9 0 0 0 a7 5*0 5 37 0 0 0 8 0 0 74 5*0 4 11*0 5 5*0
  //   52 7*0 63 9*0 36 11*0 3f 11*0 38 15*0 5 0 0 35 0 0 63 35 0 0 35 16 0 0 52 0 0 0 37 7*0 66 4*0 37 0 0
  //   0 9 3f 0 35 23 0 0 9 7*0 4 11*0 39 14 0 0 55 0 3f 0 11 7*0 73 7*0 3f 7*0 11 0 0 0 3f 0 0 0 3f 7*0 3f
  //   17*0 5 5*0 63 37 0 0 0 8 0 0 63 5*0 4 0 0 0 36 14*0 23 8*0 34 13*0 38 42 81 0 42 0 3f 0 42 9*0 34
  //   7*0 3e 5*0 42 17*0 3e 14*0 37 0 0 0 16 3f 0 0 23 0 0 16 0 0 0 31 0 0 0 4 0 0 0 13 8*0 23 6*0 23 7*0
  //   13 90*0 4f 0 4f 8*0 4f 5*0 47 0 18 0 43 14 14 4f 0 4f 4f 0 25 4f 6*0 14 0 4f 0 4f 23*0 45 11*0 43 0
  //   9 5*0 61 4f 0 0 4f 0 0 0 42 0 0 0 8 28*0 4f 10*0 4f 7*0 62 0 0 0 61 0 4f 0 49 62 31 0 42 0 0 0 29 0
  //   0 0 42 29 15*0 44 0 6 0 6 6*0 29 11*0 2 8*0 62 0 0 31 0 0 0 63 7*0 61 35*0 4f 7*0 62 0 0 0 61 43 4f
  //   6*0 27 8*0 4f 14*0 4f 0 0 4f 0 0 0 4f 0 0 0 8 11*0 2 7*0 4f 18 6*0 63 24*0 4f 0 0 0 4f 4f 0 4f 23*0
  //   4f 27 4f 5*0 63 7*0 61 116*0 52 7*0 18 4*0 58 19 20*0 52 0 0 0 45 11*0 b3 12*0 18 0 0 b3 9*0 31 29*0
  //   52 0 0 0 37 0 0 0 b3 12*0 64 10*0 b3 19*0 59 64 0 0 b3 0 0 0 21 0 0 0 b3 15*0 59 64 0 0 21 0 0 0 21
  //   28*0 56 56 5*0 56 18 7 35*0 31 18*0 74 34 0 b3 0 0 0 68 19*0 58 12 1 5*0 12 28*0 74 34 0 53 25 0 0 7
  //   0 0 0 b3 7*0 11 7*0 53 25 6*0 11 7*0 11 129*0 64 0 0 0 7 10*0 64 0 b6 0 92 10*0 63 0 18 5*0 b2 7*0
  //   61 92 95 5*0 b2 7*0 b2 0 33 14*0 64 0 73 64 b6 11 0 63 0 95 13*0 b2 0 0 0 67 0 0 0 61 73 95 0 49 69
  //   0 0 b2 7*0 b2 16*0 b6 0 0 b6 65 0 0 b2 7*0 b2 15*0 b2 69 0 0 0 6e 0 0 6f 7*0 6f 23*0 63 0 95 5*0 63
  //   0 18 5*0 b2 0 0 0 67 0 0 0 61 0 87 5*0 b2 7*0 b2 0 7 14*0 b6 4*0 66 0 b2 0 0 0 68 0 6e 0 b2 15*0 b2
  //   7*0 6f 7*0 6f 16*0 b6 0 0 b6 0 0 0 b2 0 0 0 61 0 0 0 b2 0 0 0 61 0 0 0 61 0 0 0 6e 0 0 0 b2 7*0 6f
  //   7*0 6f 85*0 74 0 0 77 0 43 0 32 8*0 47 12*0 75 0 0 47 0 0 32 6*0 74 0 47 0 47 14*0 74 0 0 15 26*0 75
  //   75 28 12*0 23 18*0 74 0 0 15 0 0 43 11*0 74 11*0 75 75 17 0 74 10*0 a2 79 0 0 74 7e 13*0 16 0 7f
  //   10*0 73 6 6*0 31 8*0 9 9 13*0 31 18*0 74 0 0 26 0 0 32 23*0 75 0 17 12*0 23 18*0 16 0 7f 27*0 28 28
  //   29*0 77 43 c1 16 a6 7f 0 0 43 23*0 43 17 17 222*0 87 0 0 87 35 0 0 87 35 0 0 35 4*0 19 0 0 31 0 0 0
  //   26 7*0 87 35 0 0 19 0 0 0 35 7*0 94 113*0 87 7*0 5 7*0 44 15*0 88 0 0 0 66 0 88 0 3 0 2 21*0 3 5*0 2
  //   23*0 87 35 0 0 26 0 0 0 53 7*0 31 15*0 53 0 44 94*0 95 0 23 95 a2 1 0 0 77 0 0 1 20*0 a2 0 0 c9 5*0
  //   93 21*0 95 64 1 0 a2 94 0 0 1 23*0 a2 92 95 0 0 8 0 0 91 0 19 22*0 64 0 0 64 94 4*0 95 13*0 92 0 0 0
  //   67 5*0 95 0 0 69 0 0 91 0 7 5*0 94 79 0 0 1 11*0 c9 4*0 76 4*0 19 13*0 3 8*0 69 19 5*0 62 23*0 95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
  //   Reset Button
endmodule
